# Fritzing sketch 104-Binary-Counter (saved by Fritzing 0.9.10b)
breadboards: 1

parts:
  S1 = DIP Switch 3 Position  # not connected
  LED1 = LED - 3mm [color="Red (633nm)" current=0.030 package="3 mm [THT]"]
  LED2 = LED - 3mm [color="Blue (430nm)" current=0.030 package="3 mm [THT]"]
  LED3 = LED - 3mm [color="Green (555nm)" current=0.030 package="3 mm [THT]"]
  LED4 = LED - 3mm [color="Yellow (585nm)" current=0.030 package="3 mm [THT]"]
  LED5 = LED - 3mm [color="Red (633nm)" current=0.030 package="3 mm [THT]"]
  LED6 = LED - 3mm [color="Blue (430nm)" current=0.030 package="3 mm [THT]"]
  LED7 = LED - 3mm [color="Green (555nm)" current=0.030 package="3 mm [THT]"]
  R1 = Resistor [tolerance=±5% power=0.25 resistance=220 package=THT]
  R2 = Resistor [tolerance=±5% power=0.25 resistance=220 package=THT]
  R3 = Resistor [tolerance=±5% power=0.25 resistance=220 package=THT]
  R4 = Resistor [tolerance=±5% power=0.25 resistance=220 package=THT]
  R5 = Resistor [tolerance=±5% power=0.25 resistance=220 package=THT]
  R6 = Resistor [tolerance=±5% power=0.25 resistance=220 package=THT]
  R7 = Resistor [tolerance=±5% power=0.25 resistance=220 package=THT]
  R8 = Resistor [tolerance=±5% power=0.25 resistance=10k package=THT]
  R9 = Resistor [tolerance=±5% power=0.25 resistance=10k package=THT]
  R10 = Resistor [tolerance=±5% power=0.25 resistance=10k package=THT]
  Part1 = Arduino Uno (Rev3) - ICSP

nets:
  N1: LED1.cathode, LED2.cathode, LED3.cathode, LED4.cathode, LED5.cathode, LED6.cathode, LED7.cathode, R8.Pin_0, R9.Pin_0, R10.Pin_0, Part1.GND
  N2: LED1.anode, R4.Pin_1
  N3: LED2.anode, R3.Pin_1
  N4: LED3.anode, R2.Pin_1
  N5: LED4.anode, R1.Pin_1
  N6: LED5.anode, R7.Pin_1
  N7: LED6.anode, R6.Pin_1
  N8: LED7.anode, R5.Pin_1
  N9: R1.Pin_0, Part1.D12/MISO
  N10: R2.Pin_0, Part1.ICSP_MOSI, Part1.D11_PWM/MOSI
  N11: R3.Pin_0, Part1.D10_PWM/SS
  N12: R4.Pin_0, Part1.D9_PWM
  N13: R5.Pin_0, Part1.D8
  N14: R6.Pin_0, Part1.D7
  N15: R7.Pin_0, Part1.D6_PWM
  N16: R8.Pin_1, Part1.D4
  N17: R9.Pin_1, Part1.D2
  N18: R10.Pin_1, Part1.D3_PWM
